# Fritzing sketch VideoPlayer (saved by Fritzing 0.9.3b)
breadboards: 1

parts:
  Raspberry_Pi_1 = Raspberry Pi 3 [part_number=RPI-3-V1.2]
  S1 = Momentary Switch [package=ksa_sealed_tac_switch]
  S2 = Momentary Switch [package=ksa_sealed_tac_switch]
  S3 = Momentary Switch [package=ksa_sealed_tac_switch]

nets:
  N1: Raspberry_Pi_1.GPIO2, S3.1
  N2: Raspberry_Pi_1.GPIO3, S1.1
  N3: Raspberry_Pi_1.GPIO4, S2.1
  N4: Raspberry_Pi_1.GND, S1.3, S2.3, S3.3
